# Fritzing sketch SensorSalinidad (saved by Fritzing 0.9.3b)
breadboards: 1

parts:
  part = SparkFun ESP8266 Thing [part_number=MCU]
  part_2 = Adafruit ADS1115 16Bit I2C ADC [part_number=ADC]
  R1 = Resistor [tolerance=±5% resistance=10k package="2010 [SMD]"]

nets:
  GND: part.GND, part_2.GND, R1.Pin_0
  N1: part.GPIO2, part_2.SDA
  N2: part.GPIO14, part_2.SCL
  N3: part.USBVCC, part_2.VDD
  N4: part_2.AIN0, R1.Pin_1

custom parts:
  Adafruit ADS1115 16Bit I2C ADC: For microcontrollers without an analog-to-digital converter or when you want a higher-precision ADC, the ADS1115 provides 16-bit precision at 860 samples/second over I2C. The chip can be configured as 4 single-ended input channels, or two differential channels. As a nice bonus, it even includes a programmable gain amplifier, up to x16, to help boost up smaller single/differential signals to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
