# Fritzing sketch Acelerómetro (saved by Fritzing 0.9.3b)
breadboards: 1

parts:
  Componente1 = SparkFun ESP8266 Thing
  M1 = gy9250

nets:
  N1: Componente1.GND, M1.pin2
  N2: Componente1.VCC, M1.pin1
  N3: Componente1.GPIO2, M1.pin4
  N4: Componente1.ADC, M1.pin7

custom parts:
  gy9250: MPU-9250 module (three-axis gyroscope + three-axis acceleration + three-axis magnetic field). The generic model from ebay et. al. rather than the Sparkfun version.
