# Fritzing sketch Acelerómetro (saved by Fritzing 0.9.3b)
breadboards: 1

parts:
  MCU_ESP8266 = SparkFun ESP8266 Thing
  MPU9250 = SparkFun IMU Breakout - MPU-9250 [part_number=" SEN-13762"]

nets:
  VCC: MCU_ESP8266.VCC, MPU9250.VDD
  N1: MCU_ESP8266.GPIO2, MPU9250.SDA/SDI
  N2: MCU_ESP8266.GPIO14, MPU9250.SCL/SCLK
  GND: MCU_ESP8266.GND, MPU9250.GND, MPU9250.AD0/SDO
  N3: MCU_ESP8266.GPIO4, MPU9250.INT
