# Fritzing sketch Pluviómetro (saved by Fritzing 0.9.3b)
breadboards: 1

parts:
  Componente2 = SparkFun ESP8266 Thing
  hc-sr2 = hc-sr04

nets:
  VCC: Componente2.VCC, hc-sr2.VCC
  GND: Componente2.GND, hc-sr2.GND
  N1: Componente2.GPIO13, hc-sr2.Trig
  N2: Componente2.GPIO12, hc-sr2.Echo

custom parts:
  hc-sr04: This is a HC-SR04 Distance Sensor
