# Fritzing sketch SensorHumedad (saved by Fritzing 0.9.3b)
breadboards: 1

parts:
  Humidity_Sensor = DFRobot Capacitive Soil Moisture Sensor V1.0 [part_number=SEN0193]
  Componente4 = Adafruit ADS1115 16Bit I2C ADC [part_number=ADC]
  Componente3 = SparkFun ESP8266 Thing [part_number=MCU]

nets:
  N1: Humidity_Sensor.A, Componente4.AIN1
  VCC: Humidity_Sensor.VCC, Componente3.VCC
  GND: Humidity_Sensor.GND, Componente4.ADDR, Componente4.GND, Componente3.GND
  N2: Componente4.SDA, Componente3.GPIO2
  N3: Componente4.SCL, Componente3.GPIO14
  N4: Componente4.VDD, Componente3.USBVCC

custom parts:
  DFRobot Capacitive Soil Moisture Sensor V1.0: DFRobot Capacitive Soil Moisture Sensor V1.0 This product measures soil moisture levels by capacitive sensing, rather than resistive sensing like other types of moisture sensor. It is made of a corrosion resistant material giving it a long service life. Insert it into soil and impress your friends with the real-time soil moisture data! The product includes an on-board voltage regulator which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
  Adafruit ADS1115 16Bit I2C ADC: For microcontrollers without an analog-to-digital converter or when you want a higher-precision ADC, the ADS1115 provides 16-bit precision at 860 samples/second over I2C. The chip can be configured as 4 single-ended input channels, or two differential channels. As a nice bonus, it even includes a programmable gain amplifier, up to x16, to help boost up smaller single/differential signals to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
