# Fritzing sketch SensorSalinidad (saved by Fritzing 0.9.3b)
breadboards: 1

parts:
  Componente1 = SparkFun ESP8266 Thing [part_number=MCU]
  Componente2 = Adafruit ADS1115 16Bit I2C ADC [part_number=ADC]
  R1 = Resistor [tolerance=±5% resistance=10k package="2010 [SMD]"]

nets (from the breadboard view):
  GND: Componente1.GND, Componente2.ADDR, Componente2.GND, R1.Pin_0
  N1: Componente1.GPIO2, Componente2.SDA
  N2: Componente1.GPIO14, Componente2.SCL
  N3: Componente1.USBVCC, Componente2.VDD
  N4: Componente2.AIN0, R1.Pin_1

custom parts:
  Adafruit ADS1115 16Bit I2C ADC: For microcontrollers without an analog-to-digital converter or when you want a higher-precision ADC, the ADS1115 provides 16-bit precision at 860 samples/second over I2C. The chip can be configured as 4 single-ended input channels, or two differential channels. As a nice bonus, it even includes a programmable gain amplifier, up to x16, to help boost up smaller single/differential signals to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
