# Fritzing sketch BMP280 (saved by Fritzing 0.9.3b)
breadboards: 1

parts:
  ESP8266 = SparkFun ESP8266 Thing
  BMP280 = Adafruit_BMP280

nets:
  GND: ESP8266.GND, BMP280.GND
  VCC: ESP8266.VCC, BMP280.VIN
  N1: ESP8266.GPIO2, BMP280.SDI/SDA
  N2: ESP8266.GPIO14, BMP280.SCK/SCL

custom parts:
  Adafruit_BMP280: Bosch has stepped up their game with their new BMP280 sensor, an environmental sensor with temperature, barometric pressure that is the next generation upgrade to the BMP085/BMP180/BMP183. This sensor is great for all sorts of weather sensing and can even be used in both I2C and SPI! This precision sensor from Bosch is the best low-cost, precision sensing solution for measuring barometric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
