# Fritzing sketch gps_receiver (saved by Fritzing 0.9.3b)
breadboards: 1

parts:
  GPS1 = GPS A2235 [package=GPS]
  MCU = SparkFun ESP8266 Thing [part_number=ESP8266]

nets:
  GND: GPS1.GND, MCU.GND
  N1: GPS1.3V3, MCU.U0TXO
  N2: GPS1.TXO, MCU.U0RXI
  N3: GPS1.RXI, MCU.GPIO15
  N4: GPS1.D15, MCU.VCC

custom parts:
  GPS A2235: Fritzing part for GPS_A2235
