# Fritzing sketch rain_gauge (saved by Fritzing 0.9.3b)
breadboards: 1

parts:
  MCU = SparkFun ESP8266 Thing [part_number="ESP8266 Thing"]
  HC-SR04 = hc-sr04 [part_number=Ultrasonic]

nets:
  VCC: MCU.VCC, HC-SR04.VCC
  GND: MCU.GND, HC-SR04.GND
  N1: MCU.GPIO5, HC-SR04.Trig
  N2: MCU.GPIO0, HC-SR04.Echo

custom parts:
  hc-sr04: This is a HC-SR04 Distance Sensor
