# Fritzing sketch salinity (saved by Fritzing 0.9.3b)
breadboards: 1

parts:
  MCU = SparkFun ESP8266 Thing [part_number="ESP8266 Thing"]
  ADC = Adafruit ADS1115 16Bit I2C ADC [part_number=ADS1115]
  R1 = Resistor [tolerance=±5% resistance=10k package="2010 [SMD]"]

nets:
  GND: MCU.GND, ADC.ADDR, ADC.GND, R1.Pin_0
  VCC: MCU.VCC, ADC.VDD
  N1: MCU.GPIO2, ADC.SDA
  N2: MCU.GPIO14, ADC.SCL
  N3: ADC.AIN0, R1.Pin_1

custom parts:
  Adafruit ADS1115 16Bit I2C ADC: For microcontrollers without an analog-to-digital converter or when you want a higher-precision ADC, the ADS1115 provides 16-bit precision at 860 samples/second over I2C. The chip can be configured as 4 single-ended input channels, or two differential channels. As a nice bonus, it even includes a programmable gain amplifier, up to x16, to help boost up smaller single/differential signals to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
