# Fritzing sketch salinity_rain_gauge_integration (saved by Fritzing 0.9.3b)
breadboards: 1

parts:
  MCU = SparkFun ESP8266 Thing [part_number="ESP8266 Thing"]
  ADC = Adafruit ADS1115 16Bit I2C ADC [part_number=ADS1115]
  R1 = Resistor [tolerance=±5% resistance=10k package=THT]
  HC-SR04 = hc-sr04 [part_number=Ultrasonic]

nets:
  GND: MCU.GND, ADC.ADDR, ADC.GND, R1.Pin_1, HC-SR04.GND
  VCC: MCU.VCC, ADC.VDD, HC-SR04.VCC
  N1: MCU.GPIO2, ADC.SDA
  N2: MCU.GPIO14, ADC.SCL
  N3: MCU.GPIO5, HC-SR04.Trig
  N4: MCU.GPIO0, HC-SR04.Echo
  N5: ADC.AIN0, R1.Pin_0

custom parts:
  Adafruit ADS1115 16Bit I2C ADC: For microcontrollers without an analog-to-digital converter or when you want a higher-precision ADC, the ADS1115 provides 16-bit precision at 860 samples/second over I2C. The chip can be configured as 4 single-ended input channels, or two differential channels. As a nice bonus, it even includes a programmable gain amplifier, up to x16, to help boost up smaller single/differential signals to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
  hc-sr04: This is a HC-SR04 Distance Sensor
