# Fritzing sketch soil_moisture (saved by Fritzing 0.9.3b)
breadboards: 1

parts:
  Soil_Moisture = DFRobot Capacitive Soil Moisture Sensor V1.0 [part_number=SEN0193]
  ADC = Adafruit ADS1115 16Bit I2C ADC [part_number=ADS1115]
  MCU = SparkFun ESP8266 Thing [part_number="ESP8266 Thing"]

nets:
  N1: Soil_Moisture.A, ADC.AIN1
  VCC: Soil_Moisture.VCC, ADC.VDD, MCU.VCC
  GND: Soil_Moisture.GND, ADC.ADDR, ADC.GND, MCU.GND
  N2: ADC.SDA, MCU.GPIO2
  N3: ADC.SCL, MCU.GPIO14

custom parts:
  DFRobot Capacitive Soil Moisture Sensor V1.0: DFRobot Capacitive Soil Moisture Sensor V1.0 This product measures soil moisture levels by capacitive sensing, rather than resistive sensing like other types of moisture sensor. It is made of a corrosion resistant material giving it a long service life. Insert it into soil and impress your friends with the real-time soil moisture data! The product includes an on-board voltage regulator which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
  Adafruit ADS1115 16Bit I2C ADC: For microcontrollers without an analog-to-digital converter or when you want a higher-precision ADC, the ADS1115 provides 16-bit precision at 860 samples/second over I2C. The chip can be configured as 4 single-ended input channels, or two differential channels. As a nice bonus, it even includes a programmable gain amplifier, up to x16, to help boost up smaller single/differential signals to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
