# Fritzing sketch wake_on_motion (saved by Fritzing 0.9.3b)
breadboards: 1

parts:
  MCU = SparkFun ESP8266 Thing [part_number="ESP8266 Thing"]
  ACCEL = SparkFun IMU Breakout - MPU-9250 [part_number=MPU9250]

nets:
  VCC: MCU.VCC, ACCEL.VDD
  N1: MCU.GPIO2, ACCEL.SDA/SDI
  N2: MCU.GPIO14, ACCEL.SCL/SCLK
  GND: MCU.GND, ACCEL.GND, ACCEL.AD0/SDO
  N3: MCU.GPIO4, ACCEL.INT
