# Fritzing sketch whole_system (saved by Fritzing 0.9.3b)

parts:
  MCU = SparkFun ESP8266 Thing [part_number="ESP8266 Thing"]
  Soil_Moisture = DFRobot Capacitive Soil Moisture Sensor V1.0 [part_number=SEN0193]
  ADC = Adafruit ADS1115 16Bit I2C ADC [part_number=ADS1115]
  R1 = Resistor [tolerance=±5% resistance=10k package="1206 [SMD]"]
  HC-SR04 = hc-sr04 [part_number=Ultrasonic]
  R2 = Resistor [tolerance=±5% resistance=2.2k package="1206 [SMD]"]
  R3 = Temperature Sensor (Thermistor) [thermistor_type=NTC package=THT]
  R4 = Resistor [tolerance=±5% resistance=10k package="1206 [SMD]"]
  A_O = LM 358 Dual Op-Amp [package="DIP8 [THT]"]
  P1 = S1133 Si Photodiode [package="8mm Ceramic [THT]"]
  Accelerometer = gy9250
  AND_GATE = SN74LVC1G08 [package=sot23-5]
  GPS1 = GPS A2235 [package=GPS]

nets:
  VCC: MCU.VCC, Soil_Moisture.VCC, ADC.VDD, HC-SR04.VCC, R3.pin_0, Accelerometer.pin1, AND_GATE.+V, GPS1.D15
  N1: MCU.GPIO2, ADC.SDA, Accelerometer.pin4
  N2: MCU.GPIO14, ADC.SCL, Accelerometer.pin3
  N3: MCU.RESET, AND_GATE.Y
  N4: MCU.U0TXO, GPS1.3V3
  N5: MCU.U0RXI, GPS1.TXO
  GND: MCU.GND, Soil_Moisture.GND, ADC.ADDR, ADC.GND, R1.Pin_0, HC-SR04.GND, A_O.connector2, A_O.connector3, P1.cathode, Accelerometer.pin2, Accelerometer.pin7, AND_GATE.GND, GPS1.GND
  N6: MCU.GPIO5, HC-SR04.Trig
  N7: MCU.GPIO0, HC-SR04.Echo
  N8: MCU.GPIO4, Accelerometer.pin8, AND_GATE.B
  N9: MCU.GPIO16, AND_GATE.A
  N10: MCU.GPIO15, GPS1.RXI
  N11: Soil_Moisture.A, ADC.AIN1
  N12: ADC.AIN3, R4.Pin_0, A_O.connector0
  N13: ADC.AIN2, R2.Pin_1
  N14: ADC.AIN0, R1.Pin_1
  N15: R2.Pin_0, R3.pin_1
  N16: R4.Pin_1, A_O.connector1, P1.anode

custom parts:
  DFRobot Capacitive Soil Moisture Sensor V1.0: DFRobot Capacitive Soil Moisture Sensor V1.0 This product measures soil moisture levels by capacitive sensing, rather than resistive sensing like other types of moisture sensor. It is made of a corrosion resistant material giving it a long service life. Insert it into soil and impress your friends with the real-time soil moisture data! The product includes an on-board voltage regulator which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
  Adafruit ADS1115 16Bit I2C ADC: For microcontrollers without an analog-to-digital converter or when you want a higher-precision ADC, the ADS1115 provides 16-bit precision at 860 samples/second over I2C. The chip can be configured as 4 single-ended input channels, or two differential channels. As a nice bonus, it even includes a programmable gain amplifier, up to x16, to help boost up smaller single/differential signals to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
  hc-sr04: This is a HC-SR04 Distance Sensor
  gy9250: MPU-9250 module (three-axis gyroscope + three-axis acceleration + three-axis magnetic field). The generic model from ebay et. al. rather than the Sparkfun version.
  GPS A2235: Fritzing part for GPS_A2235
